// Logisim project Part_B.circ as structural Verilog: 9 circuits, main circuit main
module main (
);

  wire ACCWrite, BSupported, CF, CFResult, CFWrite, clk, clock_1_out, IsShutdown, IsSupported, KK,
       maindecoder_1_issupported, MemWrite, TempSrc, TempWrite, TwoByte, Zero;
  wire [1:0] ALUSrcA, ALUSrcB, ImmSrc, PCSrc, RegDataSrc, RegSrc, RegWrite, ResultSrc;
  wire [2:0] Src1, Src2;
  wire [3:0] ACC, ALUResult, Imm, ImmA, ImmB, Reg1, Reg2, Result, ResultData, SrcA, SrcB, WSrc1;
  wire [4:0] ALUControl;
  wire [7:4] InstrA;
  wire [10:0] PC;
  wire [15:0] multiplexer_4_out, PCNext, PCPlus, PCPlus1, PCPlus2, Temp;
  wire [15:4] ImmBBB;

  Clock clock_1 (.out(clock_1_out));
  and and_1 (clk, ~IsShutdown, clock_1_out);  // AND_Gate
  Multiplexer #(.select(2), .width(16)) multiplexer_1 (
    .in0(PCPlus), .in1({ImmBBB[15:11], ImmA[2:0], ImmBBB[7:4], ImmB}),
    .in2({ImmBBB[15:12], ImmA, ImmBBB[7:4], ImmB}), .in3(Temp), .out(PCNext), .sel(PCSrc));
  Adder #(.width(16)) adder_1 (.a({ImmBBB[15:11], PC}), .b(16'h1), .out(PCPlus1));  // open: cin, cout
  Adder #(.width(16)) adder_2 (.a({ImmBBB[15:11], PC}), .b(16'h2), .out(PCPlus2));  // open: cin, cout
  Multiplexer #(.width(16)) multiplexer_2 (.in0(PCPlus1), .in1(PCPlus2), .out(PCPlus), .sel(TwoByte));
  Register #(.width(16)) u_PC (.D(PCNext), .en(1'b1), .clk(clk), .Q({ImmBBB[15:11], PC}));  // open: clr
  // Probe on PCNext
  maindecoder maindecoder_1 (
    .InstrA({InstrA, ImmA}), .InstrB({ImmBBB[7:4], ImmB}), .IsSupported(maindecoder_1_issupported),
    .ResultSrc(ResultSrc), .MemWrite(MemWrite), .ALUSrcA(ALUSrcA), .ALUSrcB(ALUSrcB), .RegSrc(RegSrc),
    .RegDataSrc(RegDataSrc), .RegWrite(RegWrite), .ACCWrite(ACCWrite), .TempWrite(TempWrite),
    .CFWrite(CFWrite), .TwoByte(TwoByte), .ImmSrc(ImmSrc), .IsShutdown(IsShutdown));
  or or_1 (IsSupported, BSupported, maindecoder_1_issupported);
  LED led_1 (.in(IsSupported));
  LED led_2 (.in(IsSupported));
  // Probe on ImmB
  instmem instmem_1 (.Address({ImmBBB[15:11], PC}), .InstrA({InstrA, ImmA}), .InstrB({ImmBBB[7:4], ImmB}));
  Comparator #(.mode("unsigned"), .width(4)) comparator_1 (.a(InstrA), .b(4'b1111), .eq(TempSrc));  // open: gt, lt
  // Probe on Result
  Register #(.width(4)) u_ACC (.D(Result), .en(ACCWrite), .clk(clk), .Q(ACC), .clr(1'b0));
  // Probe on CFResult
  Register #(.width(1)) u_CF (.D(CFResult), .en(CFWrite), .clk(clk), .Q(CF), .clr(1'b0));
  regfile regfile_1 (
    .WD1(WSrc1), .WD2(ImmB), .A1(Src1), .A2(Src2), .CLK(clk), .WE(RegWrite), .RD1(Reg1), .RD2(Reg2));  // open: Reset
  Multiplexer #(.select(2), .width(3)) multiplexer_3 (
    .in0(ImmA[3:1]), .in1(3'b000), .in2(3'b010), .in3({1'b0, InstrA[4], ImmA[3]}), .out(Src1), .sel(RegSrc));
  // Probe on PCSrc
  brancher brancher_1 (
    .InstrA({InstrA, ImmA}), .InstrB({ImmBBB[7:4], ImmB}), .CF(CF), .Zero(Zero), .KK(KK), .PCSrc(PCSrc),
    .BSupported(BSupported));
  // Probe on ACC
  Multiplexer #(.width(16)) multiplexer_4 (.in0({16{1'b0}}), .in1(PCPlus2), .out(multiplexer_4_out), .sel(TempSrc));
  LED led_3 (.in(BSupported));
  Multiplexer #(.select(2), .width(3)) multiplexer_5 (
    .in1(3'b001), .in2(3'b011), .in3(3'b100), .out(Src2), .sel(RegSrc));  // open: in0
  Register #(.width(16)) u_Temp (.D(multiplexer_4_out), .en(TempWrite), .clk(clk), .Q(Temp), .clr(1'b0));
  Multiplexer #(.select(2)) multiplexer_6 (
    .in0(ACC[0]), .in1(ACC[1]), .in2(ACC[2]), .in3(ACC[3]), .out(KK), .sel({InstrA[4], ImmA[3]}));
  Multiplexer #(.select(2), .width(4)) multiplexer_7 (
    .in0(Reg1), .in1(ACC), .in2(ResultData), .in3(4'b0000), .out(SrcA), .sel(ALUSrcA));
  Multiplexer #(.select(2), .width(4)) multiplexer_8 (
    .in0(ImmB), .in1(ImmA), .in2(4'b0001), .out(Imm), .sel(ImmSrc));  // open: in3
  // Probe on ALUControl
  aludecoder aludecoder_1 (.InstrA({InstrA, ImmA}), .InstrB({ImmBBB[7:4], ImmB}), .CF(CF), .ALUControl(ALUControl));
  alu alu_1 (
    .SrcA(SrcA), .SrcB(SrcB), .CF(CF), .ALUControl(ALUControl), .Zero(Zero), .ALUResult(ALUResult),
    .CFResult(CFResult));
  Multiplexer #(.select(2), .width(4)) multiplexer_9 (
    .in0(Reg2), .in1(ACC), .in2(Imm), .out(SrcB), .sel(ALUSrcB));  // open: in3
  // Probe on {Reg2, Reg1}
  // Probe on ALUResult
  datamem datamem_1 (.clk(clk), .WD(ALUResult), .A({Reg2, Reg1}), .WE(MemWrite), .RD(ResultData));
  // Probe on ResultData
  // Probe on ResultSrc
  Multiplexer #(.select(2), .width(4)) multiplexer_10 (
    .in0(ALUResult), .in1(ResultData), .in2(Reg1), .in3(ImmA), .out(Result), .sel(ResultSrc));
  // Probe on Result
  Multiplexer #(.select(2), .width(4)) multiplexer_11 (
    .in0(ALUResult), .in1(ACC), .in2(ImmA), .out(WSrc1), .sel(RegDataSrc));  // open: in3

  // Other names for the same wires on the sheet: PC[15:11] = ImmBBB[15:11]; ImmBBB (some bits) = {ImmA[2:0], ImmB};
  //   ImmBBBB[15:0] = {ImmBBB[15:12], ImmA, ImmBBB[7:4], ImmB}; InstrB[7:0] = {ImmBBB[7:4], ImmB}; InstrA[3:0] = ImmA
endmodule

module regfile (
  input  [2:0] A1,
  input  [2:0] A2,
  input  [3:0] WD1,
  input  [3:0] WD2,
  input  [1:0] WE,
  input  Reset,
  input  CLK,
  output [3:0] RD1,
  output [3:0] RD2
);

  wire wrA, wrA1, wrA2, wrB, wrB1, wrB2, wrC, wrC1, wrC2, wrD, wrD1, wrD2, wrE, wrE1, wrE2;
  wire [3:0] o0, o1, o2, o3, o4, WDA, WDB, WDC, WDD, WDE;

  Demultiplexer #(.select(3)) demultiplexer_1 (
    .out0(wrA1), .out1(wrB1), .out2(wrC1), .out3(wrD1), .out4(wrE1), .in(WE[0]), .sel(A1));  // open: out5, out6, out7
  Demultiplexer #(.select(3)) demultiplexer_2 (
    .out0(wrA2), .out1(wrB2), .out2(wrC2), .out3(wrD2), .out4(wrE2), .in(WE[1]), .sel(A2));  // open: out5, out6, out7
  Register #(.width(4)) RA (.D(WDA), .en(wrA), .clk(CLK), .Q(o0), .clr(1'b0));
  Register #(.width(4)) RB (.D(WDB), .en(wrB), .clk(CLK), .Q(o1), .clr(1'b0));
  Register #(.width(4)) RC (.D(WDC), .en(wrC), .clk(CLK), .Q(o2), .clr(1'b0));
  Register #(.width(4)) RD (.D(WDD), .en(wrD), .clk(CLK), .Q(o3), .clr(1'b0));
  Register #(.width(4)) RE (.D(WDE), .en(wrE), .clk(CLK), .Q(o4), .clr(1'b0));
  or or_1 (wrA, wrA1, wrA2);
  or or_2 (wrB, wrB1, wrB2);
  or or_3 (wrC, wrC1, wrC2);
  or or_4 (wrD, wrD1, wrD2);
  or or_5 (wrE, wrE1, wrE2);
  Multiplexer #(.width(4)) multiplexer_1 (.in0(WD1), .in1(WD2), .out(WDA), .sel(wrA2));
  Multiplexer #(.width(4)) multiplexer_2 (.in0(WD1), .in1(WD2), .out(WDB), .sel(wrB2));
  Multiplexer #(.width(4)) multiplexer_3 (.in0(WD1), .in1(WD2), .out(WDC), .sel(wrC2));
  Multiplexer #(.width(4)) multiplexer_4 (.in0(WD1), .in1(WD2), .out(WDD), .sel(wrD2));
  Multiplexer #(.width(4)) multiplexer_5 (.in0(WD1), .in1(WD2), .out(WDE), .sel(wrE2));
  Multiplexer #(.select(3), .width(4)) multiplexer_6 (
    .in0(o0), .in1(o1), .in2(o2), .in3(o3), .in4(o4), .out(RD1), .sel(A1));  // open: in5, in6, in7
  Multiplexer #(.select(3), .width(4)) multiplexer_7 (
    .in0(o0), .in1(o1), .in2(o2), .in3(o3), .in4(o4), .out(RD2), .sel(A2));  // open: in5, in6, in7
endmodule

module aludecoder (
  input  [7:0] InstrA,
  input  [7:0] InstrB,
  input  CF,
  output [4:0] ALUControl
);

  wire ACCDec, ACCImm, ACCInc, ACCIType, ACCITypeAdd, ACCITypeAnd, ACCITypeOr, ACCITypeSub, ACCITypeXor,
       AddCf, and_5_out, and_6_out, and_7_out, and_8_out, and_9_out, and_10_out, and_11_out, and_12_out, BCD,
       ClrCF, comparator_1_eq, comparator_2_eq, comparator_6_eq, comparator_7_eq, comparator_8_gt,
       comparator_11_eq, comparator_12_eq, comparator_13_eq, comparator_15_eq, comparator_17_eq,
       comparator_18_eq, comparator_19_eq, comparator_20_eq, comparator_21_eq, comparator_22_eq,
       comparator_23_eq, comparator_24_eq, comparator_25_eq, comparator_26_eq, Is0Opcode, Is1Opcode, IsAdd,
       IsAnd, IsOr, IsRotL, IsRotLC, IsRotR, IsRotRC, IsSub, IsXor, MbaDec, MbaInc, MdcDec, MdcInc,
       not_1_out, NotR4, OfSetCf, R4, RegDec, RegInc, RegSrc, RotOp, SetCF, SubCf, UfSetCf;

  Comparator #(.mode("unsigned")) comparator_1 (.a(InstrA), .b(8'h46), .eq(comparator_1_eq));  // open: gt, lt
  Comparator #(.mode("unsigned"), .width(4)) comparator_2 (
    .a(InstrA[7:4]), .b(4'b0100), .eq(comparator_2_eq));  // open: gt, lt
  Comparator #(.mode("unsigned")) comparator_3 (.a(InstrA), .b(8'h31), .eq(ACCInc));  // open: gt, lt
  Comparator #(.mode("unsigned")) comparator_4 (.a(InstrA), .b(8'h3f), .eq(ACCDec));  // open: gt, lt
  Comparator #(.mode("unsigned")) comparator_5 (.a(InstrA), .b(8'h36), .eq(BCD));  // open: gt, lt
  Comparator #(.mode("unsigned"), .width(7)) comparator_6 (
    .a(7'b0010101), .b(InstrA[7:1]), .eq(comparator_6_eq));  // open: gt, lt
  not not_1 (not_1_out, InstrA[0]);
  Comparator #(.mode("unsigned"), .width(4)) comparator_7 (
    .a(InstrA[7:4]), .b(4'b0001), .eq(comparator_7_eq));  // open: gt, lt
  Comparator #(.mode("unsigned"), .width(4)) comparator_8 (
    .a(InstrA[3:0]), .b(4'b1001), .gt(comparator_8_gt));  // open: eq, lt
  Comparator #(.mode("unsigned"), .width(4)) comparator_9 (
    .a(InstrA[7:4]), .b(4'b0001), .eq(Is1Opcode));  // open: gt, lt
  Comparator #(.mode("unsigned"), .width(4)) comparator_10 (.a(InstrA[7:4]), .b(4'b0111), .eq(ACCImm));  // open: gt, lt
  Comparator #(.mode("unsigned"), .width(4)) comparator_11 (
    .a(InstrA[7:4]), .b(4'b1010), .eq(comparator_11_eq));  // open: gt, lt
  Comparator #(.mode("unsigned"), .width(4)) comparator_12 (
    .a(InstrA[7:4]), .b(4'b1011), .eq(comparator_12_eq));  // open: gt, lt
  Comparator #(.mode("unsigned"), .width(4)) comparator_13 (
    .a(InstrA[7:4]), .b(4'b1101), .eq(comparator_13_eq));  // open: gt, lt
  Comparator #(.mode("unsigned"), .width(6)) comparator_14 (
    .a({InstrA[3:2], InstrA[7:4]}), .b({6{1'b0}}), .eq(RotOp));  // open: gt, lt
  not not_2 (NotR4, comparator_1_eq);
  and and_1 (R4, comparator_1_eq, comparator_2_eq);
  and and_2 (ACCIType, comparator_2_eq, NotR4);
  and and_3 (ClrCF, comparator_6_eq, not_1_out);
  and and_4 (SetCF, comparator_6_eq, InstrA[0]);
  and and_5 (and_5_out, comparator_7_eq, ~comparator_8_gt);  // AND_Gate
  Demultiplexer demultiplexer_1 (.out0(RegInc), .out1(RegDec), .in(and_5_out), .sel(InstrA[0]));
  or or_1 (RegSrc, comparator_11_eq, comparator_12_eq, comparator_13_eq);
  Demultiplexer #(.select(3)) demultiplexer_2 (
    .out0(ACCITypeAdd), .out1(ACCITypeSub), .out2(ACCITypeAnd), .out3(ACCITypeXor), .out4(ACCITypeOr),
    .in(ACCIType), .sel(InstrA[2:0]));  // open: out5, out6, out7
  Comparator #(.mode("unsigned"), .width(2)) comparator_15 (
    .a(InstrA[3:2]), .b(2'b11), .eq(comparator_15_eq));  // open: gt, lt
  Demultiplexer #(.select(2)) demultiplexer_3 (
    .out0(IsRotR), .out1(IsRotL), .out2(IsRotRC), .out3(IsRotLC), .in(RotOp), .sel(InstrA[1:0]));
  Comparator #(.mode("unsigned"), .width(4)) comparator_16 (
    .a(InstrA[7:4]), .b(4'b0000), .eq(Is0Opcode));  // open: gt, lt
  and and_6 (and_6_out, Is0Opcode, comparator_15_eq);
  Comparator #(.mode("unsigned"), .width(4)) comparator_17 (
    .a(InstrA[3:0]), .b(4'b1010), .eq(comparator_17_eq));  // open: gt, lt
  Comparator #(.mode("unsigned"), .width(4)) comparator_18 (
    .a(InstrA[3:0]), .b(4'b1101), .eq(comparator_18_eq));  // open: gt, lt
  Comparator #(.mode("unsigned"), .width(4)) comparator_19 (
    .a(InstrA[3:0]), .b(4'b1011), .eq(comparator_19_eq));  // open: gt, lt
  Comparator #(.mode("unsigned"), .width(4)) comparator_20 (
    .a(InstrA[3:0]), .b(4'b1110), .eq(comparator_20_eq));  // open: gt, lt
  Demultiplexer #(.select(2)) demultiplexer_4 (
    .out0(MbaInc), .out1(MbaDec), .out2(MdcInc), .out3(MdcDec), .in(and_6_out), .sel(InstrA[1:0]));
  and and_7 (and_7_out, Is1Opcode, comparator_17_eq);
  and and_8 (and_8_out, Is1Opcode, comparator_18_eq);
  and and_9 (and_9_out, Is1Opcode, comparator_19_eq);
  and and_10 (and_10_out, Is1Opcode, comparator_20_eq);
  or or_2 (IsAnd, and_7_out, and_8_out, ACCITypeAnd);
  or or_3 (IsXor, and_9_out, and_10_out, ACCITypeXor);
  Comparator #(.mode("unsigned"), .width(4)) comparator_21 (
    .a(InstrA[3:0]), .b(4'b1100), .eq(comparator_21_eq));  // open: gt, lt
  Comparator #(.mode("unsigned"), .width(4)) comparator_22 (
    .a(InstrA[3:0]), .b(4'b1111), .eq(comparator_22_eq));  // open: gt, lt
  Comparator #(.mode("unsigned"), .width(4)) comparator_23 (
    .a(InstrA[3:0]), .b(4'b1000), .eq(comparator_23_eq));  // open: gt, lt
  Comparator #(.mode("unsigned"), .width(4)) comparator_24 (
    .a(InstrA[3:0]), .b(4'b1001), .eq(comparator_24_eq));  // open: gt, lt
  and and_11 (and_11_out, Is1Opcode, comparator_21_eq);
  and and_12 (and_12_out, Is1Opcode, comparator_22_eq);
  and and_13 (AddCf, Is0Opcode, comparator_23_eq);
  and and_14 (OfSetCf, Is0Opcode, comparator_24_eq);
  or or_4 (IsAdd, MbaInc, ACCImm, ACCITypeAdd, RegInc, ACCInc, MdcInc);
  Priority_Encoder #(.select(5)) priority_encoder_1 (
    .in0(IsAdd), .in1(IsSub), .in2(IsAnd), .in3(IsOr), .in4(IsXor), .in5(IsRotR), .in6(IsRotL),
    .in7(IsRotRC), .in8(IsRotLC), .in9(SetCF), .in10(ClrCF), .in11(BCD), .in12(RegSrc), .in13(OfSetCf),
    .in14(UfSetCf), .in15(AddCf), .in16(SubCf), .out(ALUControl));  // open: in17, in18, in19, in20, in21, in22, in23, in24, in25, in26, in27, in28, in29, in30, in31, gs, en_out, en_in
  or or_5 (IsOr, and_11_out, and_12_out, ACCITypeOr);
  Comparator #(.mode("unsigned"), .width(4)) comparator_25 (
    .a(InstrA[3:0]), .b(4'b1010), .eq(comparator_25_eq));  // open: gt, lt
  Comparator #(.mode("unsigned"), .width(4)) comparator_26 (
    .a(InstrA[3:0]), .b(4'b1011), .eq(comparator_26_eq));  // open: gt, lt
  and and_15 (SubCf, Is0Opcode, comparator_25_eq);
  and and_16 (UfSetCf, Is0Opcode, comparator_26_eq);
  or or_6 (IsSub, MbaDec, ACCITypeSub, RegDec, ACCDec, MdcDec);

  // Other names for the same wires on the sheet: funct7[1:0] = InstrA[1:0]; funct73[3:0] = InstrA[3:0];
  //   funct3[1:0] = InstrA[3:2]; opcode[3:0] = InstrA[7:4]
endmodule

module alu (
  input  [3:0] SrcA,
  input  [3:0] SrcB,
  input  CF,
  input  [4:0] ALUControl,
  output Zero,
  output [3:0] ALUResult,
  output CFResult
);

  wire AddOf1, AddOf2, and_2_out, and_3_out, and_4_out, and_5_out, and_6_out, Bcd, comparator_1_lt,
       comparator_2_eq, comparator_3_eq, comparator_4_eq, comparator_6_eq, IsACCGE, multiplexer_3_out,
       multiplexer_4_out, multiplexer_5_out, OfOp, OfResult, or_2_out, or_4_out, or_5_out, RCLC, SubUf1,
       SubUf2, WriteCF;
  wire [3:0] adder_1_out, adder_2_out, adder_3_out, adder_4_out, and_1_out, bit_extender_1_out,
       multiplexer_1_out, or_1_out, subtractor_1_out, subtractor_2_out, subtractor_3_out, xor_1_out;

  // Probe on SrcA
  // Probe on SrcB
  Comparator #(.mode("unsigned"), .width(4)) comparator_1 (
    .a(SrcA), .b(4'b1010), .lt(comparator_1_lt));  // open: gt, eq
  assign bit_extender_1_out = {{3{1'b0}}, CF};  // Bit_Extender bit_extender_1
  Adder #(.width(4)) adder_1 (.a(SrcA), .b(SrcB), .out(adder_1_out));  // open: cin, cout
  Subtractor #(.width(4)) subtractor_1 (.a(SrcA), .b(SrcB), .out(subtractor_1_out));  // open: bin, bout
  assign and_1_out = SrcA & SrcB;  // AND_Gate and_1, 4 bits wide
  assign or_1_out = SrcA | SrcB;  // OR_Gate or_1, 4 bits wide
  assign xor_1_out = SrcA ^ SrcB;  // XOR_Gate xor_1, 4 bits wide
  Multiplexer #(.width(4)) multiplexer_1 (.in0(adder_1_out), .in1(SrcA), .out(multiplexer_1_out), .sel(and_2_out));
  and and_2 (and_2_out, comparator_1_lt, ~CF);  // AND_Gate
  Adder #(.width(4)) adder_2 (.a(SrcA), .b(SrcB), .out(adder_2_out), .cout(AddOf1));  // open: cin
  Subtractor #(.width(4)) subtractor_2 (.a(SrcB), .b(SrcA), .out(subtractor_2_out), .bout(SubUf1));  // open: bin
  Adder #(.width(4)) adder_3 (.a(SrcA), .b(SrcB), .out(adder_3_out), .cin(CF), .cout(AddOf2));
  Subtractor #(.width(4)) subtractor_3 (.a(SrcB), .b(SrcA), .out(subtractor_3_out), .bout(SubUf2));  // open: bin
  not not_1 (IsACCGE, comparator_1_lt);
  // Probe on adder_4_out
  Adder #(.width(4)) adder_4 (.a(subtractor_3_out), .b(bit_extender_1_out), .out(adder_4_out));  // open: cin, cout
  // Probe on ALUResult
  Multiplexer #(.enable("true"), .select(5), .width(4)) multiplexer_2 (
    .in0(adder_1_out), .in1(subtractor_1_out), .in2(and_1_out), .in3(or_1_out), .in4(xor_1_out),
    .in5({SrcA[0], SrcA[3:1]}), .in6({SrcA[2:0], SrcA[3]}), .in7({CF, SrcA[3:1]}), .in8({SrcA[2:0], CF}),
    .in9(4'b0001), .in10(4'b0000), .in11(multiplexer_1_out), .in12(SrcA), .in13(adder_2_out),
    .in14(subtractor_2_out), .in15(adder_3_out), .in16(adder_4_out), .out(ALUResult), .sel(ALUControl));  // open: in17, in18, in19, in20, in21, in22, in23, in24, in25, in26, in27, in28, in29, in30, in31, en
  // Probe on ALUControl
  Comparator #(.mode("unsigned"), .width(5)) comparator_2 (
    .a(ALUControl), .b(5'b00111), .eq(comparator_2_eq));  // open: gt, lt
  Comparator #(.mode("unsigned"), .width(5)) comparator_3 (
    .a(ALUControl), .b(5'b01000), .eq(comparator_3_eq));  // open: gt, lt
  or or_2 (or_2_out, ALUResult[0], ALUResult[1], ALUResult[2], ALUResult[3]);
  not not_2 (Zero, or_2_out);
  and and_3 (and_3_out, CF, ~RCLC);  // AND_Gate
  or or_3 (RCLC, comparator_2_eq, comparator_3_eq);
  and and_4 (and_4_out, comparator_2_eq, SrcA[0]);
  and and_5 (and_5_out, comparator_3_eq, SrcA[3]);
  or or_4 (or_4_out, and_3_out, and_4_out, and_5_out);
  Comparator #(.mode("unsigned"), .width(5)) comparator_4 (
    .a(ALUControl), .b(5'b01010), .eq(comparator_4_eq));  // open: gt, lt
  Comparator #(.mode("unsigned"), .width(5)) comparator_5 (.a(ALUControl), .b(5'b01011), .eq(Bcd));  // open: gt, lt
  Multiplexer multiplexer_3 (.in0(CF), .in1(or_4_out), .out(multiplexer_3_out), .sel(RCLC));
  Comparator #(.mode("unsigned"), .width(5)) comparator_6 (
    .a(ALUControl), .b(5'b01001), .eq(comparator_6_eq));  // open: gt, lt
  or or_5 (or_5_out, comparator_6_eq, comparator_4_eq, Bcd);
  and and_6 (and_6_out, Bcd, IsACCGE);
  Multiplexer #(.enable("true")) multiplexer_4 (
    .in0(ALUResult[0]), .in1(CF), .out(multiplexer_4_out), .sel(Bcd));  // open: en
  Multiplexer multiplexer_5 (.in0(multiplexer_3_out), .in1(WriteCF), .out(multiplexer_5_out), .sel(or_5_out));
  or or_6 (WriteCF, and_6_out, multiplexer_4_out);
  Multiplexer #(.enable("true")) multiplexer_6 (
    .in0(multiplexer_5_out), .in1(OfResult), .out(CFResult), .sel(OfOp));  // open: en
  // Probe on OfResult
  Multiplexer #(.enable("true"), .select(2)) multiplexer_7 (
    .in0(SubUf2), .in1(AddOf1), .in2(SubUf1), .in3(AddOf2), .out(OfResult), .sel(ALUControl[1:0]), .en(OfOp));
  // Probe on ALUControl[1:0]
  Comparator #(.mode("unsigned"), .width(5)) comparator_7 (.a(ALUControl), .b(5'b01100), .gt(OfOp));  // open: eq, lt

  // Other names for the same wires on the sheet: CFSelector[1:0] = ALUControl[1:0]; rotLC[3:0] = {SrcA[2:0], CF};
  //   rotRC[3:0] = {CF, SrcA[3:1]}; CFRC = SrcA[0]; rotL[3:0] = {SrcA[2:0], SrcA[3]};
  //   rotR[3:0] = {SrcA[0], SrcA[3:1]}; CFLC = SrcA[3]

  // Notes on the sheet:
  //   Input
  //   ALUResult
  //   Output
  //   Zero
  //   Rotate
  //   CF Operations
endmodule

module instmem (
  input  [15:0] Address,
  output [7:0] InstrA,
  output [7:0] InstrB
);

  // ROM #(.addrWidth(16), .line("dual"), .misaligned("true")) rom_1: pin names not known; wires that end beside it: Address, InstrA, InstrB

  // Notes on the sheet:
  //   // Nasty hack to make word-addressable ROM usable
  //   contents of rom_1 (hex, n*v repeats v):
  //   6e f 70 7 6f f 70 7 f2 de 6a f 78 7 f4 a5 6b 5 6 41 3 bd a0 60 a 6 22 61 a 6 20 6a f 2a 32 b8 57 32
  //   41 1 b0 31 6 41 2 b0 6d e0 57 32 41 2 b0 3d 6 41 1 b0 c6 e0 57 32 41 4 b0 49 6 41 8 b1 1c e0 57 32
  //   41 8 b0 57 6 41 4 b1 80 e0 57 e0 10 6 41 1 b8 6d 6 41 2 b8 c6 6 41 4 b9 1c 6 41 8 b9 80 e0 10 6a f
  //   71 7 62 a 6 28 21 41 f b8 81 21 41 5 36 c0 81 13 21 41 5 20 23 60 a 7 21 61 a 7 f2 16 64 3 6 50 a 1b
  //   b0 b2 65 3 6 51 a 1b b0 b2 62 a 6 41 2 b0 b2 60 a 6 22 61 a 6 20 29 5 e1 fb 60 a 6 22 61 a 6 20 4 29
  //   1a 5 29 b bd 7d 29 5 e1 fb 6a f 72 7 62 a 6 28 21 b8 d7 40 f 36 c0 d7 12 21 40 5 20 23 60 a 7 21 61
  //   a 7 f2 16 64 3 6 50 a 1b b1 8 65 3 6 51 a 1b b1 8 62 a 6 41 2 b1 8 60 a 6 22 61 a 6 20 29 5 e1 fb 60
  //   a 6 22 61 a 6 20 4 29 1a 5 29 b bd 7d 29 5 e1 fb 23 60 a 7 21 61 a 7 f2 30 6a f 74 7 62 a 6 41 1 b9
  //   40 6 41 2 b9 4a 6 41 4 b9 4d 6 41 8 b9 50 11 21 41 f b1 47 13 78 e1 53 71 e1 53 72 e1 53 74 e1 53 62
  //   a 7 60 a 23 7 61 a 21 7 62 a 6 1a b9 7b 64 3 6 50 a 1b b5 7d 65 3 6 51 a 1b b5 7d 62 a 6 41 2 b5 7d
  //   f1 ef 5 e1 fb 23 60 a 7 21 61 a 7 f2 83 6a f 78 7 62 a 6 41 1 b9 a4 6 41 2 b9 a7 6 41 4 b9 aa 6 41 8
  //   b9 ad 72 e1 b5 74 e1 b5 78 e1 b5 10 21 b1 b2 12 71 e1 b5 62 a 7 60 a 23 7 61 a 21 7 62 a 6 1a b9 dd
  //   64 3 6 50 a 1b b5 7d 65 3 6 51 a 1b b5 7d 62 a 6 41 2 b5 7d f1 ef 5 e1 fb 23 60 a 7 21 61 a 7 62 a 4
  //   7 2e 60 a 6 22 61 a 6 20 62 a 6 2e f1 e2 f5 1b 66 3 6 41 1 b2 a f5 51 e2 e f1 ef f3 4b f1 ef f4 5d
  //   f5 10 e0 10 60 a 6 22 61 a 6 20 23 41 b bd 7d 23 41 f ba 29 2e 21 42 e 0 b5 7d 2e 60 a 6 22 61 a 6
  //   20 23 41 c ba 48 23 41 d ba 5b 23 41 e ba 6b 2e 21 ba 7b 21 41 5 ba 7b 21 41 a ba 7b 21 41 f ba 7b
  //   2e 21 41 4 ba 7b 21 41 9 ba 7b 21 41 e ba 7b 2e 21 41 3 ba 7b 21 41 8 ba 7b 21 41 d ba 7b 2e 62 a 6
  //   41 1 bd 7d 2e 60 a 6 22 61 a 6 20 23 41 c ba a0 23 41 d ba b0 23 41 e ba c0 23 41 f ba d0 2e 21 41 4
  //   ba d6 21 41 9 ba d6 21 41 e ba d6 2e 21 41 3 ba d6 21 41 8 ba d6 21 41 d ba d6 2e 21 41 2 ba d6 21
  //   41 7 ba d6 21 41 c ba d6 2e 21 41 1 ba d6 2e 62 a 6 41 8 bd 7d 2e 6e f 6 62 3 7 6f f 6 63 3 7 6a 5
  //   73 7 64 6 7d 7 65 6 7a 7 66 6 74 7 64 6 6 22 65 6 6 20 66 6 6 1f 67 6 7d 7 68 6 7a 7 69 6 78 7 67 6
  //   6 22 68 6 6 20 69 6 6 1f 6a 6 7d 7 6b 6 7b 7 6c 6 71 7 60 a 7d 7 61 a 7b 7 62 a 71 7 60 a 6 22 61 a
  //   6 20 62 a 6 1f 63 a 76 7 64 a 7d 7 2e 64 6 6 22 65 6 6 20 66 6 70 1d 6a 5 6 41 1 28 64 6 29 bb 7e 27
  //   22 25 20 10 21 b3 6b 12 10 21 b3 70 12 10 21 b3 75 12 4 7 23 26 21 24 19 e3 5f 6b 5 6 bb aa 6b 5 6
  //   28 23 26 21 24 29 bb aa 27 22 25 20 10 21 b3 97 12 10 21 b3 9c 12 10 21 b3 a1 12 4 7 23 26 21 24 19
  //   e3 8b 60 a 6 5 6a 5 6 41 1 28 65 6 29 bb d5 27 22 25 20 10 21 b3 c2 12 10 21 b3 c7 12 10 21 b3 cc 12
  //   4 7 23 26 21 24 19 e3 b6 6b 5 6 bc 1 6b 5 6 28 23 26 21 24 29 bc 1 27 22 25 20 10 21 b3 ee 12 10 21
  //   b3 f3 12 10 21 b3 f8 12 4 7 23 26 21 24 19 e3 e2 61 a 6 5 6a 5 6 41 1 28 66 6 29 bc 2c 27 22 25 20
  //   10 21 b4 19 12 10 21 b4 1e 12 10 21 b4 23 12 4 7 23 26 21 24 19 e4 d 6b 5 6 bc 58 6b 5 6 28 23 26 21
  //   24 29 bc 58 27 22 25 20 10 21 b4 45 12 10 21 b4 4a 12 10 21 b4 4f 12 4 7 23 26 21 24 19 e4 39 62 a 6
  //   5 2e 6a 5 6 28 64 6 29 bc 7e 6 22 14 25 b4 6d 16 6 20 14 25 b4 74 16 6 1f 14 25 b4 7b 16 19 e4 63 6b
  //   5 6 bc a4 6b 5 6 28 61 9 29 bc a4 6 22 14 25 b4 93 16 6 20 14 25 b4 9a 16 6 1f 14 25 b4 a1 16 19 e4
  //   89 2e 60 a 6 22 61 a 6 20 61 6 23 7 62 6 21 7 63 6 4 7 60 0 52 3 4 0 0 1b 0 0 43 b 1b 55 3 5 24 53 3
  //   4 0 0 1b 0 0 43 4 1b 44 c 54 3 5 26 6 b5 2 27 43 f b4 e7 25 42 1 24 72 7 53 3 4 40 8 5 52 3 4 40 1 5
  //   61 6 6 22 62 6 6 20 63 6 6 5 2e 53 3 4 40 8 5 52 3 4 40 1 5 e4 a5 65 3 6 20 64 3 6 22 72 1f 2e 64 3
  //   6 50 a 1b b5 4c 65 3 6 51 a 1b b5 4c 62 a 6 41 2 b5 4c 62 f e 6a 5 6 41 f bd 43 e 66 3 71 7 e4 a5 6b
  //   5 e 66 3 71 7 e4 a5 66 3 70 7 2e 63 a 6 22 64 a 6 20 60 a 6 5 10 21 b5 62 12 61 a 6 5 10 21 b5 6b 12
  //   62 a 6 5 10 21 b5 74 12 63 a 23 7 64 a 21 7 2e 6d f 27 b5 85 25 bd 8f 70 7 25 b5 8b 17 3e 15 e5 7f
  //   70 7 70 20 22 24 26 28 2a 6e f 6 40 1 7 f0 8 37 3e
endmodule

module datamem (
  input  WE,
  input  [7:0] A,
  input  [3:0] WD,
  input  clk,
  output [3:0] RD
);

  wire and_1_out, and_2_out, DMX1, DMX2;
  wire [1:0] register_1_q, register_2_q, register_3_q, register_4_q, register_5_q, register_6_q,
       register_7_q, register_8_q, register_9_q, register_10_q;
  wire [3:0] R192_q, R197_q, R202_q, R207_q, R212_q, R217_q, R222_q, R227_q, R232_q, R237_q;
  wire [9:0] register_10_q_2, register_10_q_3, register_11_q, register_20_q, register_20_q_2,
       register_20_q_3, register_30_q, register_30_q_2, register_30_q_3, register_30_q_4, register_40_q,
       register_40_q_2, register_40_q_3, register_40_q_4;
  wire [30:0] demultiplexer_2_out0;
  wire [31:0] demultiplexer_3_out19;

  RAM #(.asyncread("true"), .dataWidth(4)) ram_1 (.addr(A), .we(WE), .oe(1'b1), .clk(clk), .din(WD), .dout(RD));
  and and_1 (and_1_out, A[7], A[6]);
  and and_2 (and_2_out, WE, and_1_out);
  Demultiplexer demultiplexer_1 (.out0(DMX1), .out1(DMX2), .in(and_2_out), .sel(A[5]));
  Demultiplexer #(.select(5)) demultiplexer_2 (
    .out0(demultiplexer_2_out0[0]), .out1(demultiplexer_2_out0[1]), .out2(demultiplexer_2_out0[2]),
    .out3(demultiplexer_2_out0[3]), .out4(demultiplexer_2_out0[4]), .out5(demultiplexer_2_out0[5]),
    .out6(demultiplexer_2_out0[6]), .out7(demultiplexer_2_out0[7]), .out8(demultiplexer_2_out0[8]),
    .out9(demultiplexer_2_out0[9]), .out10(demultiplexer_2_out0[10]), .out11(demultiplexer_2_out0[11]),
    .out12(demultiplexer_2_out0[12]), .out13(demultiplexer_2_out0[13]), .out14(demultiplexer_2_out0[14]),
    .out15(demultiplexer_2_out0[15]), .out16(demultiplexer_2_out0[16]), .out17(demultiplexer_2_out0[17]),
    .out18(demultiplexer_2_out0[18]), .out19(demultiplexer_2_out0[19]), .out20(demultiplexer_2_out0[20]),
    .out21(demultiplexer_2_out0[21]), .out22(demultiplexer_2_out0[22]), .out23(demultiplexer_2_out0[23]),
    .out24(demultiplexer_2_out0[24]), .out25(demultiplexer_2_out0[25]), .out26(demultiplexer_2_out0[26]),
    .out27(demultiplexer_2_out0[27]), .out28(demultiplexer_2_out0[28]), .out29(demultiplexer_2_out0[29]),
    .out30(demultiplexer_2_out0[30]), .out31(demultiplexer_3_out19[0]), .in(DMX1), .sel(A[4:0]));
  Demultiplexer #(.select(5)) demultiplexer_3 (
    .out0(demultiplexer_3_out19[0]), .out1(demultiplexer_3_out19[1]), .out2(demultiplexer_3_out19[2]),
    .out3(demultiplexer_3_out19[3]), .out4(demultiplexer_3_out19[4]), .out5(demultiplexer_3_out19[5]),
    .out6(demultiplexer_3_out19[6]), .out7(demultiplexer_3_out19[7]), .out8(demultiplexer_3_out19[8]),
    .out9(demultiplexer_3_out19[9]), .out10(demultiplexer_3_out19[10]), .out11(demultiplexer_3_out19[11]),
    .out12(demultiplexer_3_out19[12]), .out13(demultiplexer_3_out19[13]), .out14(demultiplexer_3_out19[14]),
    .out15(demultiplexer_3_out19[15]), .out16(demultiplexer_3_out19[16]), .out17(demultiplexer_3_out19[17]),
    .out18(demultiplexer_3_out19[18]), .out19(demultiplexer_3_out19[19]), .out20(demultiplexer_3_out19[20]),
    .out21(demultiplexer_3_out19[21]), .out22(demultiplexer_3_out19[22]), .out23(demultiplexer_3_out19[23]),
    .out24(demultiplexer_3_out19[24]), .out25(demultiplexer_3_out19[25]), .out26(demultiplexer_3_out19[26]),
    .out27(demultiplexer_3_out19[27]), .out28(demultiplexer_3_out19[28]), .out29(demultiplexer_3_out19[29]),
    .out30(demultiplexer_3_out19[30]), .out31(demultiplexer_3_out19[31]), .in(DMX2), .sel(A[4:0]));
  Register #(.width(4)) R192 (.D(WD), .en(demultiplexer_2_out0[0]), .clk(clk), .Q(R192_q), .clr(1'b0));
  Register #(.width(4)) R197 (.D(WD), .en(demultiplexer_2_out0[5]), .clk(clk), .Q(R197_q), .clr(1'b0));
  Register #(.width(4)) R202 (.D(WD), .en(demultiplexer_2_out0[10]), .clk(clk), .Q(R202_q), .clr(1'b0));
  Register #(.width(4)) R207 (.D(WD), .en(demultiplexer_2_out0[15]), .clk(clk), .Q(R207_q), .clr(1'b0));
  Register #(.width(4)) R212 (.D(WD), .en(demultiplexer_2_out0[20]), .clk(clk), .Q(R212_q), .clr(1'b0));
  Register #(.width(4)) R217 (.D(WD), .en(demultiplexer_2_out0[25]), .clk(clk), .Q(R217_q), .clr(1'b0));
  Register #(.width(4)) R222 (.D(WD), .en(demultiplexer_2_out0[30]), .clk(clk), .Q(R222_q), .clr(1'b0));
  Register #(.width(4)) R227 (.D(WD), .en(demultiplexer_3_out19[4]), .clk(clk), .Q(R227_q), .clr(1'b0));
  Register #(.width(4)) R232 (.D(WD), .en(demultiplexer_3_out19[9]), .clk(clk), .Q(R232_q), .clr(1'b0));
  Register #(.width(4)) R237 (.D(WD), .en(demultiplexer_3_out19[14]), .clk(clk), .Q(R237_q), .clr(1'b0));
  DotMatrix #(.matrixcols(20), .matrixrows(10)) dotmatrix_1 (
    .col0({R192_q[0], R197_q[0], R202_q[0], R207_q[0], R212_q[0], R217_q[0], R222_q[0], R227_q[0], R232_q[0], R237_q[0]}),
    .col1({R192_q[1], R197_q[1], R202_q[1], R207_q[1], R212_q[1], R217_q[1], R222_q[1], R227_q[1], R232_q[1], R237_q[1]}),
    .col2({R192_q[2], R197_q[2], R202_q[2], R207_q[2], R212_q[2], R217_q[2], R222_q[2], R227_q[2], R232_q[2], R237_q[2]}),
    .col3({R192_q[3], R197_q[3], R202_q[3], R207_q[3], R212_q[3], R217_q[3], R222_q[3], R227_q[3], R232_q[3], R237_q[3]}),
    .col4({register_1_q[0], register_2_q[0], register_3_q[0], register_4_q[0], register_5_q[0], register_6_q[0], register_7_q[0], register_8_q[0], register_9_q[0], register_10_q[0]}),
    .col5({register_1_q[1], register_2_q[1], register_3_q[1], register_4_q[1], register_5_q[1], register_6_q[1], register_7_q[1], register_8_q[1], register_9_q[1], register_10_q[1]}),
    .col6(register_10_q_2), .col7(register_10_q_3), .col8(register_11_q), .col9(register_20_q),
    .col10(register_20_q_2), .col11(register_20_q_3), .col12(register_30_q), .col13(register_30_q_2),
    .col14(register_30_q_3), .col15(register_30_q_4), .col16(register_40_q), .col17(register_40_q_2),
    .col18(register_40_q_3), .col19(register_40_q_4));
  Register #(.width(4)) register_1 (
    .D(WD), .en(demultiplexer_2_out0[1]), .clk(clk),
    .Q({register_10_q_3[9], register_10_q_2[9], register_1_q}), .clr(1'b0));
  Register #(.width(4)) register_2 (
    .D(WD), .en(demultiplexer_2_out0[6]), .clk(clk),
    .Q({register_10_q_3[8], register_10_q_2[8], register_2_q}), .clr(1'b0));
  Register #(.width(4)) register_3 (
    .D(WD), .en(demultiplexer_2_out0[11]), .clk(clk),
    .Q({register_10_q_3[7], register_10_q_2[7], register_3_q}), .clr(1'b0));
  Register #(.width(4)) register_4 (
    .D(WD), .en(demultiplexer_2_out0[16]), .clk(clk),
    .Q({register_10_q_3[6], register_10_q_2[6], register_4_q}), .clr(1'b0));
  Register #(.width(4)) register_5 (
    .D(WD), .en(demultiplexer_2_out0[21]), .clk(clk),
    .Q({register_10_q_3[5], register_10_q_2[5], register_5_q}), .clr(1'b0));
  Register #(.width(4)) register_6 (
    .D(WD), .en(demultiplexer_2_out0[26]), .clk(clk),
    .Q({register_10_q_3[4], register_10_q_2[4], register_6_q}), .clr(1'b0));
  Register #(.width(4)) register_7 (
    .D(WD), .en(demultiplexer_3_out19[0]), .clk(clk),
    .Q({register_10_q_3[3], register_10_q_2[3], register_7_q}), .clr(1'b0));
  Register #(.width(4)) register_8 (
    .D(WD), .en(demultiplexer_3_out19[5]), .clk(clk),
    .Q({register_10_q_3[2], register_10_q_2[2], register_8_q}), .clr(1'b0));
  Register #(.width(4)) register_9 (
    .D(WD), .en(demultiplexer_3_out19[10]), .clk(clk),
    .Q({register_10_q_3[1], register_10_q_2[1], register_9_q}), .clr(1'b0));
  Register #(.width(4)) register_10 (
    .D(WD), .en(demultiplexer_3_out19[15]), .clk(clk),
    .Q({register_10_q_3[0], register_10_q_2[0], register_10_q}), .clr(1'b0));
  Register #(.width(4)) register_11 (
    .D(WD), .en(demultiplexer_2_out0[2]), .clk(clk),
    .Q({register_20_q_3[9], register_20_q_2[9], register_20_q[9], register_11_q[9]}), .clr(1'b0));
  Register #(.width(4)) register_12 (
    .D(WD), .en(demultiplexer_2_out0[7]), .clk(clk),
    .Q({register_20_q_3[8], register_20_q_2[8], register_20_q[8], register_11_q[8]}), .clr(1'b0));
  Register #(.width(4)) register_13 (
    .D(WD), .en(demultiplexer_2_out0[12]), .clk(clk),
    .Q({register_20_q_3[7], register_20_q_2[7], register_20_q[7], register_11_q[7]}), .clr(1'b0));
  Register #(.width(4)) register_14 (
    .D(WD), .en(demultiplexer_2_out0[17]), .clk(clk),
    .Q({register_20_q_3[6], register_20_q_2[6], register_20_q[6], register_11_q[6]}), .clr(1'b0));
  Register #(.width(4)) register_15 (
    .D(WD), .en(demultiplexer_2_out0[22]), .clk(clk),
    .Q({register_20_q_3[5], register_20_q_2[5], register_20_q[5], register_11_q[5]}), .clr(1'b0));
  Register #(.width(4)) register_16 (
    .D(WD), .en(demultiplexer_2_out0[27]), .clk(clk),
    .Q({register_20_q_3[4], register_20_q_2[4], register_20_q[4], register_11_q[4]}), .clr(1'b0));
  Register #(.width(4)) register_17 (
    .D(WD), .en(demultiplexer_3_out19[1]), .clk(clk),
    .Q({register_20_q_3[3], register_20_q_2[3], register_20_q[3], register_11_q[3]}), .clr(1'b0));
  Register #(.width(4)) register_18 (
    .D(WD), .en(demultiplexer_3_out19[6]), .clk(clk),
    .Q({register_20_q_3[2], register_20_q_2[2], register_20_q[2], register_11_q[2]}), .clr(1'b0));
  Register #(.width(4)) register_19 (
    .D(WD), .en(demultiplexer_3_out19[11]), .clk(clk),
    .Q({register_20_q_3[1], register_20_q_2[1], register_20_q[1], register_11_q[1]}), .clr(1'b0));
  Register #(.width(4)) register_20 (
    .D(WD), .en(demultiplexer_3_out19[16]), .clk(clk),
    .Q({register_20_q_3[0], register_20_q_2[0], register_20_q[0], register_11_q[0]}), .clr(1'b0));
  Register #(.width(4)) register_21 (
    .D(WD), .en(demultiplexer_2_out0[3]), .clk(clk),
    .Q({register_30_q_4[9], register_30_q_3[9], register_30_q_2[9], register_30_q[9]}), .clr(1'b0));
  Register #(.width(4)) register_22 (
    .D(WD), .en(demultiplexer_2_out0[8]), .clk(clk),
    .Q({register_30_q_4[8], register_30_q_3[8], register_30_q_2[8], register_30_q[8]}), .clr(1'b0));
  Register #(.width(4)) register_23 (
    .D(WD), .en(demultiplexer_2_out0[13]), .clk(clk),
    .Q({register_30_q_4[7], register_30_q_3[7], register_30_q_2[7], register_30_q[7]}), .clr(1'b0));
  Register #(.width(4)) register_24 (
    .D(WD), .en(demultiplexer_2_out0[18]), .clk(clk),
    .Q({register_30_q_4[6], register_30_q_3[6], register_30_q_2[6], register_30_q[6]}), .clr(1'b0));
  Register #(.width(4)) register_25 (
    .D(WD), .en(demultiplexer_2_out0[23]), .clk(clk),
    .Q({register_30_q_4[5], register_30_q_3[5], register_30_q_2[5], register_30_q[5]}), .clr(1'b0));
  Register #(.width(4)) register_26 (
    .D(WD), .en(demultiplexer_2_out0[28]), .clk(clk),
    .Q({register_30_q_4[4], register_30_q_3[4], register_30_q_2[4], register_30_q[4]}), .clr(1'b0));
  Register #(.width(4)) register_27 (
    .D(WD), .en(demultiplexer_3_out19[2]), .clk(clk),
    .Q({register_30_q_4[3], register_30_q_3[3], register_30_q_2[3], register_30_q[3]}), .clr(1'b0));
  Register #(.width(4)) register_28 (
    .D(WD), .en(demultiplexer_3_out19[7]), .clk(clk),
    .Q({register_30_q_4[2], register_30_q_3[2], register_30_q_2[2], register_30_q[2]}), .clr(1'b0));
  Register #(.width(4)) register_29 (
    .D(WD), .en(demultiplexer_3_out19[12]), .clk(clk),
    .Q({register_30_q_4[1], register_30_q_3[1], register_30_q_2[1], register_30_q[1]}), .clr(1'b0));
  Register #(.width(4)) register_30 (
    .D(WD), .en(demultiplexer_3_out19[17]), .clk(clk),
    .Q({register_30_q_4[0], register_30_q_3[0], register_30_q_2[0], register_30_q[0]}), .clr(1'b0));
  Register #(.width(4)) register_31 (
    .D(WD), .en(demultiplexer_2_out0[4]), .clk(clk),
    .Q({register_40_q_4[9], register_40_q_3[9], register_40_q_2[9], register_40_q[9]}), .clr(1'b0));
  Register #(.width(4)) register_32 (
    .D(WD), .en(demultiplexer_2_out0[9]), .clk(clk),
    .Q({register_40_q_4[8], register_40_q_3[8], register_40_q_2[8], register_40_q[8]}), .clr(1'b0));
  Register #(.width(4)) register_33 (
    .D(WD), .en(demultiplexer_2_out0[14]), .clk(clk),
    .Q({register_40_q_4[7], register_40_q_3[7], register_40_q_2[7], register_40_q[7]}), .clr(1'b0));
  Register #(.width(4)) register_34 (
    .D(WD), .en(demultiplexer_2_out0[19]), .clk(clk),
    .Q({register_40_q_4[6], register_40_q_3[6], register_40_q_2[6], register_40_q[6]}), .clr(1'b0));
  Register #(.width(4)) register_35 (
    .D(WD), .en(demultiplexer_2_out0[24]), .clk(clk),
    .Q({register_40_q_4[5], register_40_q_3[5], register_40_q_2[5], register_40_q[5]}), .clr(1'b0));
  Register #(.width(4)) register_36 (
    .D(WD), .en(demultiplexer_2_out0[29]), .clk(clk),
    .Q({register_40_q_4[4], register_40_q_3[4], register_40_q_2[4], register_40_q[4]}), .clr(1'b0));
  Register #(.width(4)) register_37 (
    .D(WD), .en(demultiplexer_3_out19[3]), .clk(clk),
    .Q({register_40_q_4[3], register_40_q_3[3], register_40_q_2[3], register_40_q[3]}), .clr(1'b0));
  Register #(.width(4)) register_38 (
    .D(WD), .en(demultiplexer_3_out19[8]), .clk(clk),
    .Q({register_40_q_4[2], register_40_q_3[2], register_40_q_2[2], register_40_q[2]}), .clr(1'b0));
  Register #(.width(4)) register_39 (
    .D(WD), .en(demultiplexer_3_out19[13]), .clk(clk),
    .Q({register_40_q_4[1], register_40_q_3[1], register_40_q_2[1], register_40_q[1]}), .clr(1'b0));
  Register #(.width(4)) register_40 (
    .D(WD), .en(demultiplexer_3_out19[18]), .clk(clk),
    .Q({register_40_q_4[0], register_40_q_3[0], register_40_q_2[0], register_40_q[0]}), .clr(1'b0));

  // Other names for the same wires on the sheet: Addr[7:0] = A; WriteData[3:0] = WD; WriteEnable = WE

  // Notes on the sheet:
  //   // Nasty hack to make word-addressable RAM usable
endmodule

module extender (
  input  [7:0] InstrA,
  input  [7:0] InstrB,
  input  [2:0] ImmSrc,
  output [15:0] ImmExt
);

  wire [15:0] bit_extender_1_out, bit_extender_2_out, BTypeImm, JTypeImm, undriven, undriven_2, undriven_3;

  // Probe on {{6{1'b0}}, InstrA[2:0], {7{1'b0}}}
  assign bit_extender_1_out = {{8{1'b0}}, InstrB};  // Bit_Extender bit_extender_1
  // Probe on bit_extender_1_out
  Adder #(.width(16)) adder_1 (
    .a({{6{1'b0}}, InstrA[2:0], {7{1'b0}}}), .b(bit_extender_1_out), .out(BTypeImm));  // open: cin, cout
  Multiplexer #(.enable("true"), .select(3), .width(16)) multiplexer_1 (
    .in0(undriven), .in1(undriven_2), .in2(BTypeImm), .in3(JTypeImm), .in4(undriven_3), .out(ImmExt),
    .sel(ImmSrc));  // open: in5, in6, in7, en
  // Probe on {{5{1'b0}}, InstrA[3:0], {7{1'b0}}}
  assign bit_extender_2_out = {{8{1'b0}}, InstrB};  // Bit_Extender bit_extender_2
  // Probe on bit_extender_2_out
  Adder #(.width(16)) adder_2 (
    .a({{5{1'b0}}, InstrA[3:0], {7{1'b0}}}), .b(bit_extender_2_out), .out(JTypeImm));  // open: cin, cout

  // Notes on the sheet:
  //   I-type
  //   Input
  //   B-type
  //   Output
  //   S-type
  //   J-type
endmodule

module maindecoder (
  input  [7:0] InstrA,
  input  [7:0] InstrB,
  output IsSupported,
  output [1:0] ResultSrc,
  output MemWrite,
  output [1:0] ALUSrcA,
  output [1:0] ALUSrcB,
  output [1:0] RegSrc,
  output [1:0] RegDataSrc,
  output [1:0] RegWrite,
  output ACCWrite,
  output TempWrite,
  output CFWrite,
  output TwoByte,
  output [1:0] ImmSrc,
  output IsShutdown
);

  wire ACCDec, ACCImm, ACCInc, ACCIncDec, ACCIType, AccToMba, AccToMdc, and_2_out, BCD, CallRet,
       comparator_1_eq, comparator_2_eq, comparator_3_eq, comparator_4_eq, comparator_5_eq, comparator_6_eq,
       comparator_7_eq, comparator_8_eq, comparator_9_eq, comparator_10_eq, comparator_13_eq,
       comparator_14_eq, comparator_18_eq, comparator_19_eq, comparator_23_gt, comparator_24_gt,
       comparator_25_gt, comparator_29_eq, comparator_38_eq, comparator_39_eq, comparator_39_gt,
       comparator_40_lt, comparator_41_gt, comparator_42_lt, comparator_43_gt, FromMba, FromReg, IncDecMba,
       IncDecMdc, IsBbit, IsBranchACC, IsBranchREG, IsCall, IsRet, IsSupported_t, IsZeroOpcode, MbaToAcc,
       MbaToAccCf, MdcToAcc, Nop, nop_t, NotR4, or_5_out, priority_encoder_1_en_out, R4, rarb, rcrd,
       RegIncDec, RotOp, ToMba, ToReg, WCF;
  wire [4:0] Selector;

  Comparator #(.mode("unsigned")) comparator_1 (.a(InstrA), .b(8'h37), .eq(comparator_1_eq));  // open: gt, lt
  Comparator #(.mode("unsigned")) comparator_2 (.a(InstrA), .b(8'h40), .eq(comparator_2_eq));  // open: gt, lt
  Comparator #(.mode("unsigned")) comparator_3 (.a(InstrA), .b(8'h41), .eq(comparator_3_eq));  // open: gt, lt
  Comparator #(.mode("unsigned")) comparator_4 (.a(InstrA), .b(8'h42), .eq(comparator_4_eq));  // open: gt, lt
  Comparator #(.mode("unsigned")) comparator_5 (.a(InstrA), .b(8'h43), .eq(comparator_5_eq));  // open: gt, lt
  Comparator #(.mode("unsigned")) comparator_6 (.a(InstrA), .b(8'h44), .eq(comparator_6_eq));  // open: gt, lt
  Comparator #(.mode("unsigned")) comparator_7 (.a(InstrA), .b(8'h46), .eq(comparator_7_eq));  // open: gt, lt
  Comparator #(.mode("unsigned"), .width(4)) comparator_8 (
    .a(InstrA[7:4]), .b(4'b0101), .eq(comparator_8_eq));  // open: gt, lt
  Comparator #(.mode("unsigned"), .width(4)) comparator_9 (
    .a(InstrA[7:4]), .b(4'b0110), .eq(comparator_9_eq));  // open: gt, lt
  Comparator #(.mode("unsigned"), .width(4)) comparator_10 (
    .a(InstrA[7:4]), .b(4'b0001), .eq(comparator_10_eq));  // open: gt, lt
  Comparator #(.mode("unsigned"), .width(3)) comparator_11 (.a(InstrA[7:5]), .b(3'b100), .eq(IsBbit));  // open: gt, lt
  Comparator #(.mode("unsigned"), .width(4)) comparator_12 (
    .a(InstrA[7:4]), .b(4'b1011), .eq(IsBranchACC));  // open: gt, lt
  Comparator #(.mode("unsigned"), .width(4)) comparator_13 (
    .a(InstrA[7:4]), .b(4'b1010), .eq(comparator_13_eq));  // open: gt, lt
  Comparator #(.mode("unsigned"), .width(4)) comparator_14 (
    .a(InstrA[7:4]), .b(4'b1101), .eq(comparator_14_eq));  // open: gt, lt
  Comparator #(.mode("unsigned")) comparator_15 (.a(InstrA), .b(8'h3e), .eq(nop_t));  // open: gt, lt
  Comparator #(.mode("unsigned"), .width(4)) comparator_16 (.a(InstrA[7:4]), .b(4'b0110), .eq(rcrd));  // open: gt, lt
  Comparator #(.mode("unsigned"), .width(4)) comparator_17 (.a(InstrA[7:4]), .b(4'b1111), .eq(IsCall));  // open: gt, lt
  Comparator #(.mode("unsigned"), .width(2)) comparator_18 (
    .a(InstrA[3:2]), .b(2'b11), .eq(comparator_18_eq));  // open: gt, lt
  and and_1 (IsRet, comparator_18_eq, comparator_19_eq);
  Comparator #(.mode("unsigned"), .width(4)) comparator_19 (
    .a(InstrA[7:4]), .b(4'b0010), .eq(comparator_19_eq));  // open: gt, lt
  and and_2 (and_2_out, ~comparator_18_eq, comparator_19_eq);  // AND_Gate
  Comparator #(.mode("unsigned")) comparator_20 (.a(InstrA), .b(8'h4), .eq(FromMba));  // open: gt, lt
  Comparator #(.mode("unsigned")) comparator_21 (.a(InstrA), .b(8'h5), .eq(ToMba));  // open: gt, lt
  Comparator #(.mode("unsigned")) comparator_22 (.a(InstrA), .b(8'h3e), .eq(Nop));  // open: gt, lt
  or or_1 (TwoByte, comparator_1_eq, comparator_2_eq, comparator_3_eq, comparator_4_eq, comparator_5_eq, comparator_6_eq, comparator_7_eq, comparator_8_eq, comparator_9_eq, InstrA[7]);
  or or_2 (IsBranchREG, comparator_13_eq, comparator_14_eq);
  and and_3 (ToReg, and_2_out, ~InstrA[0]);  // AND_Gate
  and and_4 (FromReg, and_2_out, InstrA[0]);
  Comparator #(.mode("unsigned"), .width(4)) comparator_23 (
    .a(InstrA[3:0]), .b(4'b1001), .gt(comparator_23_gt));  // open: eq, lt
  Comparator #(.mode("unsigned"), .width(4)) comparator_24 (
    .a(InstrA[3:0]), .b(4'b1100), .gt(comparator_24_gt));  // open: eq, lt
  Comparator #(.mode("unsigned"), .width(4)) comparator_25 (
    .a(InstrA[3:0]), .b(4'b1111), .gt(comparator_25_gt));  // open: eq, lt
  Comparator #(.mode("unsigned"), .width(4)) comparator_26 (.a(InstrA[7:4]), .b(4'b0101), .eq(rarb));  // open: gt, lt
  Comparator #(.mode("unsigned"), .width(4)) comparator_27 (.a(InstrA[7:4]), .b(4'b0110), .eq(rcrd));  // open: gt, lt
  and and_5 (RegIncDec, comparator_10_eq, ~comparator_23_gt);  // AND_Gate
  and and_6 (MbaToAcc, ~comparator_24_gt, comparator_23_gt, comparator_10_eq);  // AND_Gate
  and and_7 (AccToMba, ~comparator_25_gt, comparator_24_gt, comparator_10_eq);  // AND_Gate
  or or_3 (CallRet, IsCall, IsRet);
  Comparator #(.mode("unsigned")) comparator_28 (.a(InstrA), .b(8'h46), .eq(R4));  // open: gt, lt
  Comparator #(.mode("unsigned"), .width(4)) comparator_29 (
    .a(InstrA[7:4]), .b(4'b0100), .eq(comparator_29_eq));  // open: gt, lt
  Comparator #(.mode("unsigned")) comparator_30 (.a(InstrA), .b(8'h31), .eq(ACCInc));  // open: gt, lt
  Comparator #(.mode("unsigned")) comparator_31 (.a(InstrA), .b(8'h3f), .eq(ACCDec));  // open: gt, lt
  Comparator #(.mode("unsigned"), .width(4)) comparator_32 (.a(InstrA[7:4]), .b(4'b0111), .eq(ACCImm));  // open: gt, lt
  Comparator #(.mode("unsigned")) comparator_33 (.a(InstrA), .b(8'h36), .eq(BCD));  // open: gt, lt
  Comparator #(.mode("unsigned"), .width(7)) comparator_34 (.a(InstrA[7:1]), .b(7'b0010101), .eq(WCF));  // open: gt, lt
  not not_1 (NotR4, R4);
  and and_8 (ACCIType, comparator_29_eq, NotR4);
  Comparator #(.mode("unsigned"), .width(6)) comparator_35 (
    .a({InstrA[3:2], InstrA[7:4]}), .b({6{1'b0}}), .eq(RotOp));  // open: gt, lt
  or or_4 (ACCIncDec, ACCInc, ACCDec);
  or or_5 (or_5_out, IsBbit, IsBranchACC);
  Comparator #(.mode("unsigned")) comparator_36 (.a(InstrA), .b(8'h37), .eq(IsShutdown));  // open: gt, lt
  Comparator #(.mode("unsigned"), .width(4)) comparator_37 (
    .a(InstrA[7:4]), .b(4'b0000), .eq(IsZeroOpcode));  // open: gt, lt
  Comparator #(.mode("unsigned"), .width(4)) comparator_38 (
    .a(InstrA[3:0]), .b(4'b0110), .eq(comparator_38_eq));  // open: gt, lt
  Comparator #(.mode("unsigned"), .width(4)) comparator_39 (
    .a(InstrA[3:0]), .b(4'b0111), .gt(comparator_39_gt), .eq(comparator_39_eq));  // open: lt
  Comparator #(.mode("unsigned"), .width(4)) comparator_40 (
    .a(InstrA[3:0]), .b(4'b1100), .lt(comparator_40_lt));  // open: gt, eq
  Comparator #(.mode("unsigned"), .width(4)) comparator_41 (
    .a(InstrA[3:0]), .b(4'b1011), .gt(comparator_41_gt));  // open: eq, lt
  Comparator #(.mode("unsigned"), .width(4)) comparator_42 (
    .a(InstrA[3:0]), .b(4'b1110), .lt(comparator_42_lt));  // open: gt, eq
  Comparator #(.mode("unsigned"), .width(4)) comparator_43 (
    .a(InstrA[3:0]), .b(4'b1101), .gt(comparator_43_gt));  // open: eq, lt
  or or_6 (IsSupported, IsSupported_t, IsShutdown);
  and and_9 (MdcToAcc, IsZeroOpcode, comparator_38_eq);
  and and_10 (AccToMdc, IsZeroOpcode, comparator_39_eq);
  and and_11 (MbaToAccCf, IsZeroOpcode, comparator_39_gt, comparator_40_lt);
  and and_12 (IncDecMba, comparator_41_gt, comparator_42_lt, IsZeroOpcode);
  and and_13 (IncDecMdc, comparator_43_gt, IsZeroOpcode);
  Priority_Encoder #(.select(5)) priority_encoder_1 (
    .in0(RotOp), .in1(ACCIType), .in2(R4), .in3(or_5_out), .in4(IsBranchREG), .in5(ACCIncDec), .in6(ACCImm),
    .in7(CallRet), .in8(BCD), .in9(rarb), .in10(rcrd), .in11(ToReg), .in12(FromReg), .in13(WCF),
    .in14(RegIncDec), .in15(MbaToAcc), .in16(AccToMba), .in17(MdcToAcc), .in18(AccToMdc), .in19(MbaToAccCf),
    .in20(FromMba), .in21(ToMba), .in22(IncDecMba), .in23(IncDecMdc), .in24(Nop), .out(Selector),
    .en_out(priority_encoder_1_en_out));  // open: in25, in26, in27, in28, in29, in30, in31, gs, en_in
  not not_2 (IsSupported_t, priority_encoder_1_en_out);
  // Probe on Selector
  Multiplexer #(.select(5), .width(2)) multiplexer_1 (
    .in0(2'b00), .in1(2'b00), .in5(2'b00), .in6(2'b00), .in7(2'b00), .in8(2'b00), .in12(2'b10), .in14(2'b00),
    .in15(2'b00), .in16(2'b00), .in17(2'b01), .in19(2'b00), .in20(2'b01), .in21(2'b00), .in22(2'b00),
    .in23(2'b00), .out(ResultSrc), .sel(Selector));  // open: in2, in3, in4, in9, in10, in11, in13, in18, in24, in25, in26, in27, in28, in29, in30, in31
  Multiplexer #(.select(5), .width(2)) multiplexer_2 (
    .in0(2'b00), .in1(2'b00), .in2(2'b10), .in3(2'b00), .in4(2'b00), .in5(2'b00), .in6(2'b00), .in7(2'b00),
    .in8(2'b00), .in9(2'b11), .in10(2'b11), .in11(2'b01), .in12(2'b00), .in14(2'b01), .in15(2'b00),
    .in16(2'b00), .in17(2'b00), .in18(2'b00), .in19(2'b00), .in20(2'b00), .in21(2'b00), .in22(2'b00),
    .in23(2'b00), .in24(2'b00), .out(RegWrite), .sel(Selector));  // open: in13, in25, in26, in27, in28, in29, in30, in31
  Multiplexer #(.select(5), .width(2)) multiplexer_3 (
    .in0(2'b00), .in1(2'b00), .in2(2'b11), .in4(2'b11), .in9(2'b01), .in10(2'b10), .in11(2'b00),
    .in12(2'b00), .in14(2'b00), .in15(2'b01), .in16(2'b01), .in17(2'b10), .in18(2'b10), .in19(2'b01),
    .in20(2'b01), .in21(2'b01), .in22(2'b01), .in23(2'b10), .out(RegSrc), .sel(Selector));  // open: in3, in5, in6, in7, in8, in13, in24, in25, in26, in27, in28, in29, in30, in31
  Multiplexer #(.select(5)) multiplexer_4 (
    .in0(1'b0), .in1(1'b0), .in2(1'b0), .in3(1'b0), .in4(1'b0), .in5(1'b0), .in6(1'b0), .in7(1'b0),
    .in8(1'b0), .in9(1'b0), .in10(1'b0), .in11(1'b0), .in12(1'b0), .in13(1'b0), .in14(1'b0), .in15(1'b0),
    .in16(1'b1), .in17(1'b0), .in18(1'b1), .in19(1'b0), .in20(1'b0), .in21(1'b1), .in22(1'b1), .in23(1'b1),
    .in24(1'b0), .out(MemWrite), .sel(Selector));  // open: in25, in26, in27, in28, in29, in30, in31
  Multiplexer #(.select(5)) multiplexer_5 (
    .in0(1'b1), .in1(1'b1), .in2(1'b0), .in3(1'b0), .in4(1'b0), .in5(1'b1), .in6(1'b1), .in7(1'b0),
    .in8(1'b1), .in9(1'b0), .in10(1'b0), .in11(1'b0), .in12(1'b1), .in13(1'b0), .in14(1'b0), .in15(1'b1),
    .in16(1'b0), .in17(1'b1), .in18(1'b0), .in19(1'b1), .in20(1'b1), .in21(1'b0), .in22(1'b0), .in23(1'b0),
    .in24(1'b0), .out(ACCWrite), .sel(Selector));  // open: in25, in26, in27, in28, in29, in30, in31
  Multiplexer #(.select(5)) multiplexer_6 (
    .in0(1'b0), .in1(1'b0), .in2(1'b0), .in3(1'b0), .in4(1'b0), .in5(1'b0), .in6(1'b0), .in7(1'b1),
    .in8(1'b0), .in9(1'b0), .in10(1'b0), .in11(1'b0), .in12(1'b0), .in13(1'b0), .in14(1'b0), .in15(1'b0),
    .in16(1'b0), .in17(1'b0), .in18(1'b0), .in19(1'b0), .in20(1'b0), .in21(1'b0), .in22(1'b0), .in23(1'b0),
    .in24(1'b0), .out(TempWrite), .sel(Selector));  // open: in25, in26, in27, in28, in29, in30, in31
  Multiplexer #(.select(5), .width(2)) multiplexer_7 (
    .in0(2'b01), .in1(2'b01), .in3(2'b01), .in4(2'b00), .in5(2'b01), .in6(2'b11), .in7(2'b01), .in8(2'b01),
    .in14(2'b00), .in15(2'b10), .in16(2'b10), .in18(2'b11), .in19(2'b10), .in21(2'b11), .in22(2'b10),
    .in23(2'b10), .out(ALUSrcA), .sel(Selector));  // open: in2, in9, in10, in11, in12, in13, in17, in20, in24, in25, in26, in27, in28, in29, in30, in31
  Multiplexer #(.select(5), .width(2)) multiplexer_8 (
    .in0(2'b00), .in1(2'b10), .in5(2'b10), .in6(2'b10), .in7(2'b10), .in8(2'b10), .in14(2'b10), .in15(2'b01),
    .in16(2'b01), .in18(2'b01), .in19(2'b01), .in21(2'b01), .in22(2'b10), .in23(2'b10), .out(ALUSrcB),
    .sel(Selector));  // open: in2, in3, in4, in9, in10, in11, in12, in13, in17, in20, in24, in25, in26, in27, in28, in29, in30, in31
  Multiplexer #(.select(5), .width(2)) multiplexer_9 (
    .in0(2'b00), .in1(2'b00), .in5(2'b10), .in6(2'b01), .in8(2'b01), .in14(2'b10), .in22(2'b10),
    .in23(2'b10), .out(ImmSrc), .sel(Selector));  // open: in2, in3, in4, in7, in9, in10, in11, in12, in13, in15, in16, in17, in18, in19, in20, in21, in24, in25, in26, in27, in28, in29, in30, in31
  Multiplexer #(.select(5), .width(2)) multiplexer_10 (
    .in0(2'b00), .in1(2'b00), .in9(2'b10), .in10(2'b10), .in11(2'b01), .in14(2'b00), .out(RegDataSrc),
    .sel(Selector));  // open: in2, in3, in4, in5, in6, in7, in8, in12, in13, in15, in16, in17, in18, in19, in20, in21, in22, in23, in24, in25, in26, in27, in28, in29, in30, in31
  Multiplexer #(.select(5)) multiplexer_11 (
    .in0(1'b0), .in1(1'b0), .in2(1'b0), .in3(1'b0), .in4(1'b0), .in5(1'b0), .in6(1'b0), .in7(1'b0),
    .in8(1'b1), .in9(1'b0), .in10(1'b0), .in11(1'b0), .in12(1'b0), .in13(1'b1), .in14(1'b0), .in15(1'b0),
    .in16(1'b0), .in17(1'b0), .in18(1'b0), .in19(1'b1), .in20(1'b0), .in21(1'b0), .in22(1'b0), .in23(1'b0),
    .in24(1'b0), .out(CFWrite), .sel(Selector));  // open: in25, in26, in27, in28, in29, in30, in31

  // Other names for the same wires on the sheet: opcode[3:0] = InstrA[7:4]; opcode3b[2:0] = InstrA[7:5];
  //   funct3[1:0] = InstrA[3:2]; funct73[3:0] = InstrA[3:0]; funct7[1:0] = InstrA[1:0]; Shutdown = IsShutdown

  // Notes on the sheet:
  //   Input
  //   Helpers
  //   Output
  //   Control Signals
endmodule

module brancher (
  input  [7:0] InstrA,
  input  [7:0] InstrB,
  input  CF,
  input  Zero,
  input  KK,
  output [1:0] PCSrc,
  output BSupported
);

  wire and_2_out, and_3_out, and_4_out, and_5_out, and_6_out, Branch, comparator_2_eq, comparator_3_eq,
       comparator_4_eq, IsBbit, IsBnez, IsBranchCF, IsBranchREG, IsCall, IsJump, IsRet, not_1_out, or_2_out,
       xor_1_out;

  Comparator #(.mode("unsigned"), .width(3)) comparator_1 (.a(InstrA[7:5]), .b(3'b100), .eq(IsBbit));  // open: gt, lt
  Comparator #(.mode("unsigned"), .width(4)) comparator_2 (
    .a(InstrA[7:4]), .b(4'b1011), .eq(comparator_2_eq));  // open: gt, lt
  Comparator #(.mode("unsigned"), .width(4)) comparator_3 (
    .a(InstrA[7:4]), .b(4'b1010), .eq(comparator_3_eq));  // open: gt, lt
  Comparator #(.mode("unsigned"), .width(4)) comparator_4 (
    .a(InstrA[7:4]), .b(4'b1101), .eq(comparator_4_eq));  // open: gt, lt
  Comparator #(.mode("unsigned"), .width(4)) comparator_5 (
    .a(InstrA[7:4]), .b(4'b1100), .eq(IsBranchCF));  // open: gt, lt
  Comparator #(.mode("unsigned"), .width(4)) comparator_6 (.a(InstrA[7:4]), .b(4'b1110), .eq(IsJump));  // open: gt, lt
  Comparator #(.mode("unsigned"), .width(4)) comparator_7 (.a(InstrA[7:4]), .b(4'b1111), .eq(IsCall));  // open: gt, lt
  Comparator #(.mode("unsigned")) comparator_8 (.a(InstrA), .b(8'h2e), .eq(IsRet));  // open: gt, lt
  and and_1 (IsBnez, comparator_2_eq, InstrA[3]);
  or or_1 (IsBranchREG, and_2_out, comparator_3_eq, comparator_4_eq);
  // Probe on InstrA[7:4]
  and and_2 (and_2_out, ~InstrA[3], comparator_2_eq);  // AND_Gate
  or or_2 (or_2_out, IsJump, IsCall);
  and and_3 (and_3_out, IsBbit, KK);
  and and_4 (and_4_out, IsBranchREG, ~Zero);  // AND_Gate
  and and_5 (and_5_out, Zero, IsBnez);
  and and_6 (and_6_out, IsBranchCF, not_1_out);
  not not_1 (not_1_out, xor_1_out);
  xor xor_1 (xor_1_out, CF, InstrA[3]);
  or or_3 (Branch, and_3_out, and_4_out, and_5_out, and_6_out);
  or or_4 (BSupported, IsBbit, IsBnez, IsBranchREG, IsBranchCF, IsJump, IsCall, IsRet);
  Priority_Encoder #(.select(2)) priority_encoder_1 (
    .in0(1'b1), .in1(Branch), .in2(or_2_out), .in3(IsRet), .out(PCSrc));  // open: gs, en_out, en_in
  // Probe on PCSrc

  // Other names for the same wires on the sheet: BranchSupported = BSupported; opcode[3:0] = InstrA[7:4];
  //   opcode3b[2:0] = InstrA[7:5]
endmodule
